# Fritzing sketch alarm_clock (saved by Fritzing 0.9.1b)
breadboards: 1

parts:
  Part1 = Arduino Uno (Rev3)
  LCD1 = LCD screen
  R1 = Rotary Potentiometer (Small) [maximum_resistance=10kΩ package=THT]
  J1 = Piezo Speaker
  LED1 = LED - 3mm [color="Red (633nm)" package="3 mm [THT]"]
  S1 = Momentary Switch [package=ksa_sealed_tac_switch]
  S2 = Momentary Switch [package=ksa_sealed_tac_switch]

nets (from the breadboard view):
  N1: Part1.D8, LED1.cathode
  N2: Part1.D11_PWM/MOSI, LCD1.E
  N3: Part1.D12/MISO, LCD1.RS
  N4: Part1.D2, LCD1.DB7
  N5: Part1.D3_PWM, LCD1.DB6
  N6: Part1.D4, LCD1.DB5
  N7: Part1.D5_PWM, LCD1.DB4
  N8: Part1.D6_PWM, S2.1
  N9: Part1.D7, S1.1
  5V: Part1.5V, LCD1.VDD, R1.leg2
  GND: Part1.GND, LCD1.VSS, LCD1.R/W, R1.leg1, J1.pin1, S1.3, S2.3
  N10: LCD1.V0, R1.wiper
  N11: J1.pin2, LED1.anode
